# Fritzing sketch analog_read (saved by Fritzing 0.9.10b)
breadboards: 1

parts:
  Microcontroller = Arduino Uno (Rev3) - ICSP
  R3 = PHOTOCELL [package=photocell-kit]
  R2 = Resistor [tolerance=±5% power=0.25 resistance=1k package=THT]

nets:
  N1: Microcontroller.A0, R3.P$2, R2.Pin_1
  N2: Microcontroller.GND, R3.P$1
  N3: Microcontroller.5V, R2.Pin_0
