# Fritzing sketch circuit0_1 (saved by Fritzing 0.9.10b)
breadboards: 1

parts:
  LED1 = smd LED [color="Red (633nm)" package="0603 [SMD]"]
  Microcontroller = Arduino Uno (Rev3) - ICSP
  R1 = Resistor [tolerance=±5% resistance=220 power=0.25 package=THT]
  S1 = Pushbutton [package="[SMD]"]

nets:
  N1: LED1.cathode, R1.Pin_1
  N2: LED1.anode, S1.Pin_3, S1.Pin_4
  N3: Microcontroller.GND, R1.Pin_0
  N4: Microcontroller.5V, S1.Pin_1, S1.Pin_2
