# Fritzing sketch circuit0_1_bad_no_output (saved by Fritzing 0.9.10b)
breadboards: 1

parts:
  Microcontroller = Arduino Uno (Rev3) - ICSP
  S1 = Pushbutton [package="[SMD]"]

nets:
  N1: Microcontroller.D2, S1.Pin_3, S1.Pin_4
  N2: Microcontroller.5V, S1.Pin_1, S1.Pin_2
