# Fritzing sketch circuit2 (saved by Fritzing 0.9.10b)
breadboards: 1

parts:
  Microcontroller = Arduino Uno (Rev3) - ICSP
  R1 = Resistor [tolerance=±5% resistance=220 power=0.25 package=THT]
  LED1 = smd LED [color="Red (633nm)" package="0603 [SMD]"]

nets:
  N1: Microcontroller.GND, R1.Pin_0
  N2: Microcontroller.D9_PWM, LED1.anode
  N3: R1.Pin_1, LED1.cathode
