# Fritzing sketch circuit2_1 (saved by Fritzing 0.9.10b)
breadboards: 1

parts:
  Microcontroller = Arduino Uno (Rev3) - ICSP
  R1 = Resistor [tolerance=±5% resistance=220 power=0.25 package=THT]
  LED1 = RGB LED (com. cathode, rgb) [package="5 mm [THT]"]
  R3 = Resistor [tolerance=±5% resistance=220 power=0.25 package=THT]
  R2 = Resistor [tolerance=±5% power=0.25 resistance=220 package=THT]

nets:
  N1: Microcontroller.D3_PWM, R1.Pin_0
  N2: Microcontroller.D5_PWM, R3.Pin_1
  N3: Microcontroller.D6_PWM, R2.Pin_1
  N4: Microcontroller.GND, LED1.common_cathode
  N5: R1.Pin_1, LED1.red_anode
  N6: LED1.green_anode, R3.Pin_0
  N7: LED1.blue_anode, R2.Pin_0
