# Fritzing sketch circuit3 (saved by Fritzing 0.9.10b)
breadboards: 1

parts:
  LED1 = smd LED [color="Red (633nm)" package="0603 [SMD]"]
  Microcontroller = Arduino Uno (Rev3) - ICSP
  R1 = Resistor [tolerance=±5% resistance=220 power=0.25 package=THT]
  S1 = Pushbutton [package="[SMD]"]
  R2 = Resistor [tolerance=±5% resistance=10k power=0.25 package=THT]

nets:
  N1: LED1.cathode, R1.Pin_1
  N2: LED1.anode, Microcontroller.D13/SCK
  N3: Microcontroller.GND, R1.Pin_0, S1.Pin_1, S1.Pin_2
  N4: Microcontroller.D2, S1.Pin_3, S1.Pin_4, R2.Pin_1
  N5: Microcontroller.5V, R2.Pin_0
