# Fritzing sketch circuit5 (saved by Fritzing 0.9.10b)
breadboards: 1

parts:
  LED1 = smd LED [color="Red (633nm)" package="0603 [SMD]"]
  LED3 = smd LED [color="Yellow (585nm)" package="0603 [SMD]"]
  Part1 = Arduino Uno (Rev3) - ICSP
  R1 = Resistor [tolerance=±5% resistance=220 package="0805 [SMD]"]
  R2 = Resistor [tolerance=±5% resistance=220 package="0805 [SMD]"]
  R3 = Resistor [tolerance=±5% resistance=220 package="0805 [SMD]"]
  R4 = Resistor [tolerance=±5% resistance=220 package="0805 [SMD]"]
  R5 = Resistor [tolerance=±5% resistance=220 package="0805 [SMD]"]
  R6 = Resistor [tolerance=±5% resistance=220 package="0805 [SMD]"]
  R7 = Resistor [tolerance=±5% resistance=10k package="0805 [SMD]"]
  R8 = Resistor [tolerance=±5% resistance=10k package="0805 [SMD]"]
  LED4 = RGB LED (com. cathode, rgb) [package="5 mm [THT]"]
  S3 = Pushbutton [package="[SMD]"]
  S4 = Pushbutton [package="[SMD]"]
  LED5 = smd LED [color="Green (565nm)" package="0603 [SMD]"]
  R10 = TRIMPOT [maximum_resistance=20kΩ knob_status=50% power=0.5W package=trimpot_pth_s3_lock]

nets (from the schematic view):
  N1: LED1.cathode, R1.Pin_0
  N2: LED1.anode, Part1.D13/SCK
  N3: LED3.cathode, R3.Pin_0
  N4: LED3.anode, Part1.D11_PWM/MOSI
  N5: Part1.A0, R10.WIPER
  N6: Part1.D9_PWM, R6.Pin_0
  N7: Part1.D12/MISO, LED5.anode
  N8: Part1.GND, R1.Pin_1, R2.Pin_1, R3.Pin_1, LED4.common_cathode, S3.Pin_1, S3.Pin_2, S4.Pin_1, S4.Pin_2, R10.CCW
  N9: Part1.D2, R7.Pin_0, S4.Pin_3, S4.Pin_4
  N10: Part1.D3_PWM, R8.Pin_0, S3.Pin_3, S3.Pin_4
  N11: Part1.D5_PWM, R4.Pin_1
  N12: Part1.D6_PWM, R5.Pin_0
  N13: Part1.5V, R7.Pin_1, R8.Pin_1, R10.CW
  N14: R2.Pin_0, LED5.cathode
  N15: R4.Pin_0, LED4.red_anode
  N16: R5.Pin_1, LED4.green_anode
  N17: R6.Pin_1, LED4.blue_anode
