# Fritzing sketch if_tester (saved by Fritzing 0.9.10b)
breadboards: 1

parts:
  LED1 = smd LED [color="Red (633nm)" package="0603 [SMD]"]
  MCU = Arduino Uno (Rev3) - ICSP
  R1 = Resistor [tolerance=±5% resistance=220 package="0805 [SMD]"]
  R2 = Resistor [tolerance=±5% resistance=220 package="0805 [SMD]"]
  LED5 = smd LED [color="Green (565nm)" package="0603 [SMD]"]

nets:
  N1: LED1.cathode, R1.Pin_0
  N2: LED1.anode, MCU.D13/SCK
  N3: MCU.D12/MISO, LED5.anode
  N4: MCU.GND, R1.Pin_1, R2.Pin_1
  N5: R2.Pin_0, LED5.cathode
