# Fritzing sketch pullup (saved by Fritzing 0.9.10b)
breadboards: 1

parts:
  Microcontroller = Arduino Uno (Rev3) - ICSP
  S1 = Pushbutton [package="[SMD]"]
  R2 = Resistor [tolerance=±5% resistance=10k power=0.25 package=THT]

nets:
  N1: Microcontroller.GND, S1.Pin_1, S1.Pin_2
  N2: Microcontroller.D2, S1.Pin_3, S1.Pin_4, R2.Pin_1
  N3: Microcontroller.5V, R2.Pin_0
