# Fritzing sketch switch_right (saved by Fritzing 0.9.10b)
breadboards: 1

parts:
  S1 = Pushbutton [package="[SMD]"]
  R1 = Resistor [tolerance=±5% resistance=10k power=0.25 package=THT]
  Microcontroller = Arduino Uno (Rev3) - ICSP

nets:
  N1: S1.Pin_1, S1.Pin_2, Microcontroller.GND
  N2: S1.Pin_3, S1.Pin_4, R1.Pin_1, Microcontroller.D2
  N3: R1.Pin_0, Microcontroller.5V
