# Fritzing sketch voltage_divider (saved by Fritzing 0.9.10b)
breadboards: 1

parts:
  Microcontroller = Arduino Uno (Rev3) - ICSP
  R2 = Resistor [tolerance=±5% resistance=10k power=0.25 package=THT]
  R3 = PHOTOCELL [package=photocell-kit]

nets:
  N1: Microcontroller.A0, R2.Pin_1, R3.P$2
  N2: Microcontroller.GND, R3.P$1
  N3: Microcontroller.5V, R2.Pin_0
